// Logisim project Multiplier.circ as structural Verilog: 2 circuits, main circuit Multiplier
module Multiplier (
  input  in_1,
  input  in_2,
  input  in_3,
  input  in_4
);

  wire and_1_out, and_2_out, and_3_out, and_4_out, half_adder_1_out_3, half_adder_1_out_4,
       half_adder_2_out_3, half_adder_2_out_4, n7448_1_p8, n7448_1_p9, n7448_1_p10, n7448_1_p11, n7448_1_p12,
       n7448_1_p13, n7448_1_p14;

  and and_1 (and_1_out, in_3, in_1);
  and and_2 (and_2_out, in_2, in_3);
  and and_3 (and_3_out, in_1, in_4);
  and and_4 (and_4_out, in_4, in_2);
  Half_adder half_adder_1 (.in_1(and_2_out), .in_2(and_3_out), .out_3(half_adder_1_out_3), .out_4(half_adder_1_out_4));
  Half_adder half_adder_2 (
    .in_1(half_adder_1_out_4), .in_2(and_4_out), .out_3(half_adder_2_out_3), .out_4(half_adder_2_out_4));
  // _7448 7448_1: pin names not known; wires that end beside it: half_adder_1_out_3, half_adder_2_out_3, 1'b1, half_adder_2_out_4, and_1_out, 1'b0, 1'b1, n7448_1_p8, n7448_1_p9, n7448_1_p10, n7448_1_p11, n7448_1_p12, n7448_1_p13, n7448_1_p14
  _7_Segment_Display u_7_segment_display_1 (
    .g(n7448_1_p9), .f(n7448_1_p8), .a(n7448_1_p10), .b(n7448_1_p11), .e(n7448_1_p14), .d(n7448_1_p13),
    .c(n7448_1_p12));  // open: dp
endmodule

module Half_adder (
  input  in_1,
  input  in_2,
  output out_3,
  output out_4
);

  xor xor_1 (out_3, in_1, in_2);
  and and_1 (out_4, in_1, in_2);
endmodule
